# Fritzing sketch Covid-19 Wearable (saved by Fritzing 0.9.9b)
breadboards: 1

parts:
  Vibratory_Motor = Vibration Motor- ROB-08449 [package=vibe-motor-10mm]
  NPN_Transistor = NPN-Transistor [package="TO92 [THT]"]
  BAT1 = Battery Holders [package=battery-aa]
  LED1 = smd LED [color="Red (633nm)" package="0603 [SMD]"]
  R1 = Resistor [tolerance=±5% resistance=220 package="2010 [SMD]"]
  Tilt_Switch = Tilt Switch [package=THT]
  U2 = attiny85 [package=dip]
  Switch = Toggle Switch [package=THT]

nets:
  N1: Vibratory_Motor.+, NPN_Transistor.E
  N2: Vibratory_Motor.-, NPN_Transistor.C, BAT1.-, LED1.cathode, Tilt_Switch.Pin_1, U2.Pin_4
  N3: NPN_Transistor.B, U2.Pin_5
  N4: BAT1.+, Switch.L1
  N5: LED1.anode, R1.Pin_0
  N6: R1.Pin_1, U2.Pin_3
  N7: Tilt_Switch.Pin_2, U2.Pin_2
  N8: U2.Pin_8, Switch.COM
